// Logisim project Amoo_LogisimPractice.circ as structural Verilog: 1 circuit, main circuit main
module main (
  input  Circuit_Tutorial,
  input  in_2,
  input  in_3,
  output out_4
);

  wire and_1_out, and_2_out;

  and and_1 (and_1_out, Circuit_Tutorial, in_2);
  and and_2 (and_2_out, in_2, in_3);
  and and_3 (out_4, and_1_out, and_2_out);
endmodule
