// Logisim project Amoo_ThreeSensorSecurityAlarm.circ as structural Verilog: 1 circuit, main circuit main
module main (
  input  D,
  input  W,
  input  M,
  output A
);

  wire and_1_out, and_2_out, and_3_out, and_4_out, not_1_out, not_2_out, not_3_out;

  not not_1 (not_1_out, D);
  not not_2 (not_2_out, W);
  not not_3 (not_3_out, M);
  and and_1 (and_1_out, not_1_out, W, M);
  and and_2 (and_2_out, D, not_2_out, M);
  and and_3 (and_3_out, D, W, not_3_out);
  and and_4 (and_4_out, D, W, M);
  or or_1 (A, and_1_out, and_2_out, and_3_out, and_4_out);
endmodule
