// Logisim project Practice.circ as structural Verilog: 1 circuit, main circuit main
module main (
  input  in_1,
  input  in_2,
  input  in_3,
  output out_4
);

  wire and_1_out, and_2_out, and_3_out, and_4_out, and_5_out, and_6_out, and_7_out, and_8_out;

  and and_1 (and_1_out, in_1, in_2, in_3);
  not not_1 (in_2, in_2);
  buf and_2 (and_2_out, in_1);  // AND_Gate
  // AND_Gate and_3 has open pins: out=and_3_out
  // AND_Gate and_4 has open pins: out=and_4_out
  // AND_Gate and_5 has open pins: out=and_5_out
  // AND_Gate and_6 has open pins: out=and_6_out
  // AND_Gate and_7 has open pins: out=and_7_out
  // AND_Gate and_8 has open pins: out=and_8_out
  or or_1 (out_4, and_1_out, and_2_out, and_3_out, and_4_out, and_5_out, and_6_out, and_7_out, and_8_out);

  // Notes on the sheet:
  //   \((\neg A \wedge B \wedge \neg C) \vee (\neg A \wedge B \wedge C) \vee (A \wedge B \wedge \neg C) \vee (A \wedge B \wedge C) \vee (\neg A \wedge B \wedge C) \vee (A \wedge \neg B \wedge C) \vee (A \wedge B \wedge C) \vee (\neg A \wedge \neg B \wedge \neg C)\)
endmodule
